# Fritzing sketch traffic_lights (saved by Fritzing 0.7.0b)
breadboards: 1

parts:
  Arduino1 = Arduino
  R1 = Resistor [tolerance=±5% resistance=220 package=THT]
  R2 = Resistor [tolerance=±5% resistance=220 package=THT]
  R3 = Resistor [tolerance=±5% resistance=220 package=THT]
  LED1 = LED - 5mm [color="Red (633nm)" package="5 mm [THT]"]
  LED3 = LED - 5mm [color="Green (565nm)" package="5 mm [THT]"]
  LED2 = LED - 5mm [color="Yellow (585nm)" package="5 mm [THT]"]

nets:
  N1: Arduino1.D11, R1.Pin_0
  N2: Arduino1.D10, R2.Pin_0
  N3: Arduino1.D9, R3.Pin_0
  N4: Arduino1.GND, LED1.cathode, LED3.cathode, LED2.cathode
  N5: R1.Pin_1, LED1.anode
  N6: R2.Pin_1, LED2.anode
  N7: R3.Pin_1, LED3.anode
